// Logisim project ULA.circ as structural Verilog: 6 circuits, main circuit main
module main (
  input  in_1,
  input  [2:0] in_2,
  input  [2:0] in_3
);

  wire somador_completo_1_carry, somador_completo_2_carry, subtrador_completo_1_bout,
       subtrador_completo_2_bout;
  wire [3:0] somador_completo_1_r, subtrador_completo_1_r;

  somador_completo somador_completo_1 (
    .C(in_1), .A(in_2[0]), .B(in_3[0]), .R(somador_completo_1_r[0]), .Carry(somador_completo_1_carry));
  somador_completo somador_completo_2 (
    .C(somador_completo_1_carry), .A(in_2[1]), .B(in_3[1]), .R(somador_completo_1_r[1]),
    .Carry(somador_completo_2_carry));
  somador_completo somador_completo_3 (
    .C(somador_completo_2_carry), .A(in_2[2]), .B(in_3[2]), .R(somador_completo_1_r[2]),
    .Carry(somador_completo_1_r[3]));
  subtrador_completo subtrador_completo_1 (
    .Bin(in_1), .A(in_2[0]), .B(in_3[0]), .R(subtrador_completo_1_r[0]), .Bout(subtrador_completo_1_bout));
  subtrador_completo subtrador_completo_2 (
    .Bin(subtrador_completo_1_bout), .A(in_2[1]), .B(in_3[1]), .R(subtrador_completo_1_r[1]),
    .Bout(subtrador_completo_2_bout));
  subtrador_completo subtrador_completo_3 (
    .Bin(subtrador_completo_2_bout), .A(in_2[2]), .B(in_3[2]), .R(subtrador_completo_1_r[2]),
    .Bout(subtrador_completo_1_r[3]));
  Hex_Digit_Display hex_digit_display_1 (.value(somador_completo_1_r));  // open: dp
  Hex_Digit_Display hex_digit_display_2 (.value(subtrador_completo_1_r));  // open: dp
endmodule

// Som
module somador_completo (
  input  C,
  input  A,
  input  B,
  output R,
  output Carry
);

  wire and_1_out, and_2_out, xor_1_out, xor_2_out;

  xor xor_1 (xor_1_out, A, B);
  xor xor_2 (xor_2_out, A, B);
  xor xor_3 (R, xor_1_out, C);
  and and_1 (and_1_out, xor_2_out, C);
  or or_1 (Carry, and_1_out, and_2_out);
  and and_2 (and_2_out, A, B);
endmodule

// Sub
module subtrador_completo (
  input  Bin,
  input  A,
  input  B,
  output R,
  output Bout
);

  wire and_1_out, and_2_out, not_1_out, xor_1_out, xor_3_out;

  xor xor_1 (xor_1_out, A, B);
  xor xor_2 (R, xor_1_out, Bin);
  xor xor_3 (xor_3_out, B, Bin);
  and and_1 (and_1_out, xor_3_out, not_1_out);
  not not_1 (not_1_out, A);
  and and_2 (and_2_out, B, Bin);
  or or_1 (Bout, and_1_out, and_2_out);
endmodule

module teste (
  input  A,
  input  B,
  input  C,
  output R,
  output out_5
);

  wire and_1_out, and_2_out, not_1_out, xor_1_out, xor_3_out;

  xor xor_1 (xor_1_out, A, B);
  xor xor_2 (R, xor_1_out, C);
  xor xor_3 (xor_3_out, B, C);
  not not_1 (not_1_out, A);
  and and_1 (and_1_out, B, C);
  and and_2 (and_2_out, xor_3_out, not_1_out);
  or or_1 (out_5, and_2_out, and_1_out);
endmodule

module multiplicador (
  input  [7:0] in_1,
  input  [7:0] in_2,
  input  [2:0] in_3,
  input  in_4
);

  wire and_1_out, and_2_out, button_1_out, clock_1_out, d_ff_1_q, d_ff_2_q, d_ff_3_q, d_ff_4_q,
       multiplexer_1_out, not_1_out, somador_4_bits_1_r0, somador_4_bits_1_r1, somador_4_bits_1_r2,
       somador_4_bits_1_r3, undriven;
  wire [2:0] and_5_out, Contador_q;
  wire [2:2] or_1_out;
  wire [7:0] and_10_out, shifter_1_out;

  Clock clock_1 (.out(clock_1_out));
  and and_1 (and_1_out, clock_1_out, not_1_out);
  D_Flip_Flop d_ff_1 (
    .clk(clock_1_out), .D(somador_4_bits_1_r3), .Q(d_ff_1_q), .en(undriven));  // open: Qn, preset, reset
  Counter #(.width(3), .max('h7)) Contador (
    .Q(Contador_q), .clk(and_1_out), .clr(button_1_out));  // open: load, D, count, carry
  Button button_1 (.out(button_1_out));
  not not_1 (not_1_out, and_2_out);
  or or_1 (or_1_out[2], Contador_q[2], Contador_q[1], Contador_q[0]);
  and and_2 (and_2_out, Contador_q[2], Contador_q[1], Contador_q[0]);
  D_Flip_Flop d_ff_2 (
    .clk(clock_1_out), .D(somador_4_bits_1_r2), .Q(d_ff_2_q), .en(undriven));  // open: Qn, preset, reset
  // NOT_Gate not_2 is placed but not wired
  Multiplexer #(.select(3)) multiplexer_1 (
    .in0(in_2[0]), .in1(in_2[1]), .in2(in_2[2]), .in3(in_2[3]), .in4(in_2[4]), .in5(in_2[5]), .in6(in_2[6]),
    .in7(in_2[7]), .out(multiplexer_1_out), .sel(Contador_q), .en(in_4));
  D_Flip_Flop d_ff_3 (
    .clk(clock_1_out), .D(somador_4_bits_1_r1), .Q(d_ff_3_q), .en(undriven));  // open: Qn, preset, reset
  and and_3 (and_10_out[7], in_1[7], multiplexer_1_out);
  and and_4 (and_10_out[6], in_1[6], multiplexer_1_out);
  assign and_5_out = in_3 & {3{or_1_out[2]}};  // AND_Gate and_5, 3 bits wide
  D_Flip_Flop d_ff_4 (
    .clk(clock_1_out), .D(somador_4_bits_1_r0), .Q(d_ff_4_q), .en(undriven));  // open: Qn, preset, reset
  and and_6 (and_10_out[4], in_1[4], multiplexer_1_out);
  and and_7 (and_10_out[5], in_1[5], multiplexer_1_out);
  Shifter shifter_1 (.in(and_10_out), .\dist (and_5_out), .out(shifter_1_out));
  somador_4_bits somador_4_bits_1 (
    .A3(d_ff_1_q), .B3(shifter_1_out[3]), .A2(d_ff_2_q), .B2(shifter_1_out[2]), .A1(d_ff_3_q),
    .B1(shifter_1_out[1]), .A0(d_ff_4_q), .B0(shifter_1_out[0]), .R3(somador_4_bits_1_r3),
    .R2(somador_4_bits_1_r2), .R1(somador_4_bits_1_r1), .R0(somador_4_bits_1_r0));  // open: C
  and and_8 (and_10_out[2], in_1[2], multiplexer_1_out);
  and and_9 (and_10_out[3], in_1[3], multiplexer_1_out);
  and and_10 (and_10_out[0], in_1[0], multiplexer_1_out);
  and and_11 (and_10_out[1], in_1[1], multiplexer_1_out);
endmodule

module somador_4_bits (
  input  A3,
  input  B3,
  input  A2,
  input  B2,
  input  A1,
  input  B1,
  input  A0,
  input  B0,
  output C,
  output R3,
  output R2,
  output R1,
  output R0
);

  wire somador_completo_2_carry, somador_completo_3_carry, somador_completo_4_carry;

  somador_completo somador_completo_1 (.C(somador_completo_3_carry), .A(B3), .B(A3), .R(R3), .Carry(C));
  somador_completo somador_completo_2 (
    .C(somador_completo_4_carry), .A(B1), .B(A1), .R(R1), .Carry(somador_completo_2_carry));
  somador_completo somador_completo_3 (
    .C(somador_completo_2_carry), .A(B2), .B(A2), .R(R2), .Carry(somador_completo_3_carry));
  somador_completo somador_completo_4 (.C(1'b0), .A(B0), .B(A0), .R(R0), .Carry(somador_completo_4_carry));
endmodule
